# Fritzing sketch AKS (saved by Fritzing 0.9.3b)

parts:
  Parça1 = Arduino Due (Rev2b)
  Parça2 = InvenSense MPU6050
  M2 = DC Motor
  8_Channel_Relay1 = 8 Channel Power Relay
  R1 = Resistor [tolerance=±5% resistance=10k package="0402 [SMD]"]
  S1 = Round Pushbutton
  R2 = Resistor [tolerance=±5% resistance=10k package="0402 [SMD]"]
  S2 = Round Pushbutton
  S3 = Round Pushbutton
  LED1 = LED - 5mm [color="Red (633nm)" package="5 mm [THT]"]
  LED2 = LED - 5mm [color="Red (633nm)" package="5 mm [THT]"]
  LED3 = LED - 5mm [color="Red (633nm)" package="5 mm [THT]"]
  R4 = Resistor [tolerance=±5% resistance=10k package="0402 [SMD]"]
  S4 = Round Pushbutton
  Parça3 = Arduino Mega 2560 (Rev3)
  R3 = Resistor [tolerance=±5% resistance=10k package="0402 [SMD]"]
  R5 = Resistor [tolerance=±5% resistance=10k package="0402 [SMD]"]
  S5 = Round Pushbutton
  LED5 = smd LED [color="Red (633nm)" package="1206 [SMD]"]
  LED6 = smd LED [color="Red (633nm)" package="1206 [SMD]"]
  LED8 = smd LED [color="Red (633nm)" package="1206 [SMD]"]
  J1 = Infrared Proximity Sensor  # not connected
  R6 = Resistor [tolerance=±5% resistance=1k package="0805 [SMD]"]
  YL-83_-_Detection_Board1 = YL-83 Rain Sensor - Detection Board
  YL-83_-_Control_Board1 = YL-83 Rain Sensor - Control Board
  R7 = Resistor [tolerance=±5% resistance=10k package="0402 [SMD]"]  # not connected
  Parça4 = XBee USB Mini Adapter
  D2F1 = D2F-FL Omron Snap Action Limit Switch with Level
  D2F2 = D2F-FL Omron Snap Action Limit Switch with Level
  D2F3 = D2F-FL Omron Snap Action Limit Switch with Level
  R9 = Resistor [tolerance=±5% resistance=220 package="0402 [SMD]"]  # not connected
  U1 = Nokia 6100 Color LCD [package=nokia6100_lcd]
  M1 = RioRand LM2596
  VCC1 = Battery block 9V
  VCC2 = Battery

nets:
  N1: Parça1.A0, YL-83_-_Control_Board1.AO
  N2: Parça1.D14/TX3, U1.CS
  N3: Parça1.D15/RX3, U1.SCK
  N4: Parça1.D17/RX2, Parça4.RXD
  N5: Parça1.D18/TX1, Parça3.D19/RX1
  N6: Parça1.D19/RX1, Parça3.D18/TX1
  N7: Parça1.GND, S1.leg0, S2.leg0, S4.leg0, S5.leg0, M1.Pin_4
  N8: Parça1.D8_PWM, 8_Channel_Relay1.IN5
  N9: Parça1.D9_PWM, 8_Channel_Relay1.IN4
  N10: Parça1.D10_PWM/SS0, 8_Channel_Relay1.IN3
  N11: Parça1.D11_PWM, 8_Channel_Relay1.IN2
  N12: Parça1.D12_PWM, 8_Channel_Relay1.IN1
  N13: Parça1.D13_PWM, Parça2.INT
  N14: Parça1.SDA1, Parça2.SDA
  N15: Parça1.SCL1, Parça2.SCL
  N16: Parça1.D2_PWM, R6.Pin_1
  N17: Parça1.D5_PWM, 8_Channel_Relay1.IN8
  N18: Parça1.D6_PWM, 8_Channel_Relay1.IN7
  N19: Parça1.D7_PWM, 8_Channel_Relay1.IN6
  N20: Parça1.D33, D2F3.NC
  N21: Parça2.VCC, R4.Pin_0, M1.Pin_3
  N22: M2.pin_1, 8_Channel_Relay1.COM#43
  N23: M2.pin_2, 8_Channel_Relay1.NO#44
  N24: 8_Channel_Relay1.GND, VCC2.-
  N25: 8_Channel_Relay1.VCC, 8_Channel_Relay1.JD-VCC, 8_Channel_Relay1.NO#41, LED1.anode, VCC1.+
  N26: 8_Channel_Relay1.COM#28, LED6.cathode
  N27: 8_Channel_Relay1.NO#29, LED6.anode
  N28: 8_Channel_Relay1.COM#31, LED5.cathode
  N29: 8_Channel_Relay1.NO#32, LED5.anode
  N30: 8_Channel_Relay1.COM#34, LED3.cathode, LED8.cathode
  N31: 8_Channel_Relay1.NO#35, LED3.anode, LED8.anode
  N32: 8_Channel_Relay1.COM#37, LED2.cathode
  N33: 8_Channel_Relay1.NO#38, LED2.anode
  N34: 8_Channel_Relay1.COM#40, LED1.cathode
  N35: R1.Pin_1, S1.leg1
  N36: R2.Pin_1, S2.leg1
  N37: S3.leg1, R3.Pin_1
  N38: R4.Pin_1, S4.leg1
  N39: R5.Pin_0, D2F1.COM
  N40: R5.Pin_1, S5.leg1
  N41: YL-83_-_Detection_Board1.POS, YL-83_-_Control_Board1.POS
  N42: YL-83_-_Detection_Board1.NEG, YL-83_-_Control_Board1.NEG
  N43: D2F1.NO, D2F2.COM
  N44: D2F2.NO, D2F3.COM

notes:
  WIPER MOTOR
  MPU 6050
  WIPER
  BUTTON
  FRONT
  HEADLIGHT
  BUTTON
  FRONT
  HEADLIGHT
  REAR
  LIGHT
  BRAKE
  RIGHT
  SIGNAL
  BUTTON
  IN-VEHICLE
  LIGHTING
  IN-VEHICLE
  LIGHTING
  BUTTON
  BMS BOX
  LEFT
  SIGNAL
  BUTTON
  REAR LIGHT RIGHT SIGNAL
  REAR
  LIGHT
  LEFT
  SIGNAL
  Proximity Sensor(It symbolically drawn.)
  Our Sensor Connecting:
  -Blue(GND)
  -Brown(VCC) +12V
  -Black(Signal)
  (for the RPM calculating)
  RAIN SENSOR
  XBEE
  SAFETY BELT SWITCHES
  NEXTION LCD SCREEN
  -BLACK(GND)
  -RED(+5 VCC)
  -PINK(TX)
  -BLUE(RX)

custom parts:
  8 Channel Power Relay: An 8 channel power relay. The module operates at 5V.
  YL-83 Rain Sensor - Detection Board: The YL-83 is a rain sensor that has more resistance when dry and less resistance when wet. The module runs at 5V.
  YL-83 Rain Sensor - Control Board: The YL-83 is a rain sensor that has more resistance when dry and less resistance when wet. The module runs at 5V.
  D2F-FL Omron Snap Action Limit Switch with Level: Snap action switch with stainless steel lever.
